// Logisim project alu_milestone1.circ as structural Verilog: 24 circuits, main circuit ALU8
module NOT (
  input  A,
  output Y
);

  Transistor #(.\type ("p")) transistor_1 (.in(1'b1), .out(Y), .gate(A));
  Transistor #(.\type ("n")) transistor_2 (.in(1'b0), .out(Y), .gate(A));
endmodule

module NAND (
  input  A,
  input  B,
  output Y
);

  wire transistor_4_out, undriven, undriven_2;

  Transistor #(.\type ("p")) transistor_1 (.in(1'b1), .out(Y), .gate(undriven));
  Transistor #(.\type ("p")) transistor_2 (.in(1'b1), .out(Y), .gate(undriven_2));
  Transistor #(.\type ("n")) transistor_3 (.in(transistor_4_out), .out(Y), .gate(B));
  Transistor #(.\type ("n")) transistor_4 (.in(1'b0), .out(transistor_4_out), .gate(A));
endmodule

module NOR (
  input  A,
  input  B,
  output Y
);

  wire transistor_1_out, undriven, undriven_2;

  Transistor #(.\type ("p")) transistor_1 (.in(1'b1), .out(transistor_1_out), .gate(undriven));
  Transistor #(.\type ("p")) transistor_2 (.in(transistor_1_out), .out(Y), .gate(undriven_2));
  Transistor #(.\type ("n")) transistor_3 (.in(1'b0), .out(Y), .gate(A));
  Transistor #(.\type ("n")) transistor_4 (.in(1'b0), .out(Y), .gate(B));
endmodule

module AND (
  input  A,
  input  B,
  output Y
);

  wire nand_1_y;

  NAND nand_1 (.A(A), .B(B), .Y(nand_1_y));
  NOT not_1 (.A(nand_1_y), .Y(Y));
endmodule

module OR (
  input  A,
  input  B,
  output Y
);

  wire nor_1_y;

  NOR nor_1 (.A(A), .B(B), .Y(nor_1_y));
  NOT not_1 (.A(nor_1_y), .Y(Y));
endmodule

module XOR (
  input  A,
  input  B,
  output Y
);

  wire nand_1_y, nand_2_y, nand_3_y, undriven, undriven_2, undriven_3, undriven_4;

  NAND nand_1 (.A(undriven_3), .B(undriven), .Y(nand_1_y));
  NAND nand_2 (.A(A), .B(undriven_4), .Y(nand_2_y));
  NAND nand_3 (.A(undriven_2), .B(nand_1_y), .Y(nand_3_y));
  NAND nand_4 (.A(nand_2_y), .B(nand_3_y), .Y(Y));
endmodule

module XNOR (
  input  A,
  input  B,
  output Y
);

  wire xor_1_y;

  XOR xor_1 (.A(A), .B(B), .Y(xor_1_y));
  NOT not_1 (.A(xor_1_y), .Y(Y));
endmodule

module AND3 (
  input  A,
  input  B,
  input  C,
  output Y
);

  wire and_1_y;

  AND and_1 (.A(A), .B(B), .Y(and_1_y));
  AND and_2 (.A(and_1_y), .B(C), .Y(Y));
endmodule

module OR3 (
  input  A,
  input  B,
  input  C,
  output Y
);

  wire or_1_y;

  OR or_1 (.A(A), .B(B), .Y(or_1_y));
  OR or_2 (.A(or_1_y), .B(C), .Y(Y));
endmodule

module HALFADD (
  input  A,
  input  B,
  output S,
  output C
);

  wire undriven, undriven_2;

  XOR xor_1 (.A(A), .B(B), .Y(S));
  AND and_1 (.A(undriven), .B(undriven_2), .Y(C));
endmodule

module ODD (
  input  A,
  input  B,
  input  Cin,
  output Y
);

  wire xor_1_y;

  XOR xor_1 (.A(A), .B(B), .Y(xor_1_y));
  XOR xor_2 (.A(xor_1_y), .B(Cin), .Y(Y));
endmodule

module MAJ (
  input  A,
  input  B,
  input  Cin,
  output Y
);

  wire and_1_y, and_2_y, and_3_y, undriven, undriven_2, undriven_3;

  AND and_1 (.A(A), .B(B), .Y(and_1_y));
  AND and_2 (.A(undriven), .B(Cin), .Y(and_2_y));
  AND and_3 (.A(undriven_2), .B(undriven_3), .Y(and_3_y));
  OR3 or3_1 (.A(and_1_y), .B(and_2_y), .C(and_3_y), .Y(Y));
endmodule

module FULLADD (
  input  A,
  input  B,
  input  Cin,
  output S,
  output Cout
);

  wire undriven, undriven_2, undriven_3;

  ODD odd_1 (.A(A), .B(B), .Cin(Cin), .Y(S));
  MAJ maj_1 (.A(undriven), .B(undriven_2), .Cin(undriven_3), .Y(Cout));
endmodule

module ADD8 (
  input  A0,
  input  A1,
  input  A2,
  input  A3,
  input  A4,
  input  A5,
  input  A6,
  input  A7,
  input  B0,
  input  B1,
  input  B2,
  input  B3,
  input  B4,
  input  B5,
  input  B6,
  input  B7,
  input  Cin,
  output S0,
  output S1,
  output S2,
  output S3,
  output S4,
  output S5,
  output S6,
  output S7,
  output Cout
);

  wire fulladd_1_cout, fulladd_2_cout, fulladd_3_cout, fulladd_4_cout, fulladd_5_cout, fulladd_6_cout,
       fulladd_7_cout;

  FULLADD fulladd_1 (.A(A0), .B(B0), .Cin(Cin), .S(S0), .Cout(fulladd_1_cout));
  FULLADD fulladd_2 (.A(A1), .B(B1), .Cin(fulladd_1_cout), .S(S1), .Cout(fulladd_2_cout));
  FULLADD fulladd_3 (.A(A2), .B(B2), .Cin(fulladd_2_cout), .S(S2), .Cout(fulladd_3_cout));
  FULLADD fulladd_4 (.A(A3), .B(B3), .Cin(fulladd_3_cout), .S(S3), .Cout(fulladd_4_cout));
  FULLADD fulladd_5 (.A(A4), .B(B4), .Cin(fulladd_4_cout), .S(S4), .Cout(fulladd_5_cout));
  FULLADD fulladd_6 (.A(A5), .B(B5), .Cin(fulladd_5_cout), .S(S5), .Cout(fulladd_6_cout));
  FULLADD fulladd_7 (.A(A6), .B(B6), .Cin(fulladd_6_cout), .S(S6), .Cout(fulladd_7_cout));
  FULLADD fulladd_8 (.A(A7), .B(B7), .Cin(fulladd_7_cout), .S(S7), .Cout(Cout));
endmodule

module AND8 (
  input  A0,
  input  A1,
  input  A2,
  input  A3,
  input  A4,
  input  A5,
  input  A6,
  input  A7,
  input  B0,
  input  B1,
  input  B2,
  input  B3,
  input  B4,
  input  B5,
  input  B6,
  input  B7,
  output Y0,
  output Y1,
  output Y2,
  output Y3,
  output Y4,
  output Y5,
  output Y6,
  output Y7
);

  AND and_1 (.A(A0), .B(B0), .Y(Y0));
  AND and_2 (.A(A1), .B(B1), .Y(Y1));
  AND and_3 (.A(A2), .B(B2), .Y(Y2));
  AND and_4 (.A(A3), .B(B3), .Y(Y3));
  AND and_5 (.A(A4), .B(B4), .Y(Y4));
  AND and_6 (.A(A5), .B(B5), .Y(Y5));
  AND and_7 (.A(A6), .B(B6), .Y(Y6));
  AND and_8 (.A(A7), .B(B7), .Y(Y7));
endmodule

module XOR8 (
  input  A0,
  input  A1,
  input  A2,
  input  A3,
  input  A4,
  input  A5,
  input  A6,
  input  A7,
  input  B0,
  input  B1,
  input  B2,
  input  B3,
  input  B4,
  input  B5,
  input  B6,
  input  B7,
  output Y0,
  output Y1,
  output Y2,
  output Y3,
  output Y4,
  output Y5,
  output Y6,
  output Y7
);

  XOR xor_1 (.A(A0), .B(B0), .Y(Y0));
  XOR xor_2 (.A(A1), .B(B1), .Y(Y1));
  XOR xor_3 (.A(A2), .B(B2), .Y(Y2));
  XOR xor_4 (.A(A3), .B(B3), .Y(Y3));
  XOR xor_5 (.A(A4), .B(B4), .Y(Y4));
  XOR xor_6 (.A(A5), .B(B5), .Y(Y5));
  XOR xor_7 (.A(A6), .B(B6), .Y(Y6));
  XOR xor_8 (.A(A7), .B(B7), .Y(Y7));
endmodule

module OR8 (
  input  i0,
  input  i1,
  input  i2,
  input  i3,
  input  i4,
  input  i5,
  input  i6,
  input  i7,
  output Y
);

  wire or_1_y, or_2_y, or_3_y, or_4_y, or_5_y, or_6_y;

  OR or_1 (.A(i0), .B(i1), .Y(or_1_y));
  OR or_2 (.A(or_1_y), .B(i2), .Y(or_2_y));
  OR or_3 (.A(or_2_y), .B(i3), .Y(or_3_y));
  OR or_4 (.A(or_3_y), .B(i4), .Y(or_4_y));
  OR or_5 (.A(or_4_y), .B(i5), .Y(or_5_y));
  OR or_6 (.A(or_5_y), .B(i6), .Y(or_6_y));
  OR or_7 (.A(or_6_y), .B(i7), .Y(Y));
endmodule

module DECODER3 (
  input  S0,
  input  S1,
  input  S2,
  output D0,
  output D1,
  output D2,
  output D3,
  output D4,
  output D5,
  output D6,
  output D7
);

  wire not_1_y, not_2_y, not_3_y, undriven, undriven_2, undriven_3, undriven_4, undriven_5, undriven_6,
       undriven_7, undriven_8, undriven_9, undriven_10, undriven_11, undriven_12, undriven_13, undriven_14,
       undriven_15, undriven_16, undriven_17, undriven_18, undriven_19, undriven_20, undriven_21;

  NOT not_1 (.A(S0), .Y(not_1_y));
  NOT not_2 (.A(S1), .Y(not_2_y));
  NOT not_3 (.A(S2), .Y(not_3_y));
  AND3 and3_1 (.A(undriven), .B(undriven_2), .C(undriven_3), .Y(D0));
  AND3 and3_2 (.A(undriven_4), .B(undriven_5), .C(undriven_6), .Y(D1));
  AND3 and3_3 (.A(undriven_7), .B(undriven_8), .C(undriven_9), .Y(D2));
  AND3 and3_4 (.A(undriven_10), .B(undriven_11), .C(not_3_y), .Y(D3));
  AND3 and3_5 (.A(undriven_12), .B(undriven_13), .C(undriven_14), .Y(D4));
  AND3 and3_6 (.A(undriven_15), .B(not_2_y), .C(undriven_16), .Y(D5));
  AND3 and3_7 (.A(not_1_y), .B(undriven_17), .C(undriven_18), .Y(D6));
  AND3 and3_8 (.A(undriven_19), .B(undriven_20), .C(undriven_21), .Y(D7));
endmodule

module DEMUX3 (
  input  S0,
  input  S1,
  input  S2,
  input  X,
  output Y0,
  output Y1,
  output Y2,
  output Y3,
  output Y4,
  output Y5,
  output Y6,
  output Y7
);

  wire decoder3_1_d0, decoder3_1_d1, decoder3_1_d2, decoder3_1_d3, decoder3_1_d4, decoder3_1_d5,
       decoder3_1_d6, decoder3_1_d7, undriven, undriven_2, undriven_3, undriven_4, undriven_5, undriven_6,
       undriven_7;

  DECODER3 decoder3_1 (
    .S0(S0), .S1(S1), .S2(S2), .D0(decoder3_1_d0), .D1(decoder3_1_d1), .D2(decoder3_1_d2),
    .D3(decoder3_1_d3), .D4(decoder3_1_d4), .D5(decoder3_1_d5), .D6(decoder3_1_d6), .D7(decoder3_1_d7));
  AND and_1 (.A(decoder3_1_d0), .B(X), .Y(Y0));
  AND and_2 (.A(decoder3_1_d1), .B(undriven), .Y(Y1));
  AND and_3 (.A(decoder3_1_d2), .B(undriven_2), .Y(Y2));
  AND and_4 (.A(decoder3_1_d3), .B(undriven_3), .Y(Y3));
  AND and_5 (.A(decoder3_1_d4), .B(undriven_4), .Y(Y4));
  AND and_6 (.A(decoder3_1_d5), .B(undriven_5), .Y(Y5));
  AND and_7 (.A(decoder3_1_d6), .B(undriven_6), .Y(Y6));
  AND and_8 (.A(decoder3_1_d7), .B(undriven_7), .Y(Y7));
endmodule

module DECDEMUX3 (
  input  S0,
  input  S1,
  input  S2,
  input  X,
  output D0,
  output D1,
  output D2,
  output D3,
  output D4,
  output D5,
  output D6,
  output D7,
  output Y0,
  output Y1,
  output Y2,
  output Y3,
  output Y4,
  output Y5,
  output Y6,
  output Y7
);

  wire decoder3_1_d0, decoder3_1_d1, decoder3_1_d2, decoder3_1_d3, decoder3_1_d4, decoder3_1_d5,
       decoder3_1_d6, decoder3_1_d7, undriven, undriven_2, undriven_3, undriven_4, undriven_5, undriven_6,
       undriven_7;

  DECODER3 decoder3_1 (
    .S0(S0), .S1(S1), .S2(S2), .D0(decoder3_1_d0), .D1(decoder3_1_d1), .D2(decoder3_1_d2),
    .D3(decoder3_1_d3), .D4(decoder3_1_d4), .D5(decoder3_1_d5), .D6(decoder3_1_d6), .D7(decoder3_1_d7));
  AND and_1 (.A(D0), .B(X), .Y(Y0));
  AND and_2 (.A(D1), .B(undriven), .Y(Y1));
  AND and_3 (.A(D2), .B(undriven_2), .Y(Y2));
  AND and_4 (.A(D3), .B(undriven_3), .Y(Y3));
  AND and_5 (.A(D4), .B(undriven_4), .Y(Y4));
  AND and_6 (.A(D5), .B(undriven_5), .Y(Y5));
  AND and_7 (.A(D6), .B(undriven_6), .Y(Y6));
  AND and_8 (.A(D7), .B(undriven_7), .Y(Y7));
endmodule

module MUX1_8 (
  input  d0,
  input  d1,
  input  d2,
  input  d3,
  input  d4,
  input  d5,
  input  d6,
  input  d7,
  input  s0,
  input  s1,
  input  s2,
  input  s3,
  input  s4,
  input  s5,
  input  s6,
  input  s7,
  output Y
);

  wire and_1_y, and_2_y, and_3_y, and_4_y, and_5_y, and_6_y, and_7_y, and_8_y;

  AND and_1 (.A(d0), .B(s0), .Y(and_1_y));
  AND and_2 (.A(d1), .B(s1), .Y(and_2_y));
  AND and_3 (.A(d2), .B(s2), .Y(and_3_y));
  AND and_4 (.A(d3), .B(s3), .Y(and_4_y));
  AND and_5 (.A(d4), .B(s4), .Y(and_5_y));
  AND and_6 (.A(d5), .B(s5), .Y(and_6_y));
  AND and_7 (.A(d6), .B(s6), .Y(and_7_y));
  AND and_8 (.A(d7), .B(s7), .Y(and_8_y));
  OR8 or8_1 (
    .i0(and_1_y), .i1(and_2_y), .i2(and_3_y), .i3(and_4_y), .i4(and_5_y), .i5(and_6_y), .i6(and_7_y),
    .i7(and_8_y), .Y(Y));
endmodule

module LSHIFT8 (
  input  A0,
  input  A1,
  input  A2,
  input  A3,
  input  A4,
  input  A5,
  input  A6,
  input  A7,
  output Y0,
  output Y1,
  output Y2,
  output Y3,
  output Y4,
  output Y5,
  output Y6,
  output Y7
);


  assign Y0 = 1'b0;
  assign Y1 = A0;
  assign Y2 = A1;
  assign Y3 = A2;
  assign Y4 = A3;
  assign Y5 = A4;
  assign Y6 = A5;
  assign Y7 = A6;
endmodule

module RSHIFT8 (
  input  A0,
  input  A1,
  input  A2,
  input  A3,
  input  A4,
  input  A5,
  input  A6,
  input  A7,
  output Y0,
  output Y1,
  output Y2,
  output Y3,
  output Y4,
  output Y5,
  output Y6,
  output Y7
);


  assign Y0 = A1;
  assign Y1 = A2;
  assign Y2 = A3;
  assign Y3 = A4;
  assign Y4 = A5;
  assign Y5 = A6;
  assign Y6 = A7;
  assign Y7 = 1'b0;
endmodule

module ALU8 (
  input  A0,
  input  A1,
  input  A2,
  input  A3,
  input  A4,
  input  A5,
  input  A6,
  input  A7,
  input  B0,
  input  B1,
  input  B2,
  input  B3,
  input  B4,
  input  B5,
  input  B6,
  input  B7,
  input  selADD,
  input  selSUB,
  input  selAND,
  input  selXOR,
  input  selLSH,
  input  selRSH,
  output R0,
  output R1,
  output R2,
  output R3,
  output R4,
  output R5,
  output R6,
  output R7,
  output Cout
);

  wire add8_1_s0, add8_1_s1, add8_1_s2, add8_1_s3, add8_1_s4, add8_1_s5, add8_1_s6, add8_1_s7, and8_1_y0,
       and8_1_y1, and8_1_y2, and8_1_y3, and8_1_y4, and8_1_y5, and8_1_y6, and8_1_y7, lshift8_1_y0,
       lshift8_1_y1, lshift8_1_y2, lshift8_1_y3, lshift8_1_y4, lshift8_1_y5, lshift8_1_y6, lshift8_1_y7,
       rshift8_1_y0, rshift8_1_y1, rshift8_1_y2, rshift8_1_y3, rshift8_1_y4, rshift8_1_y5, rshift8_1_y6,
       rshift8_1_y7, undriven, undriven_2, undriven_3, undriven_4, undriven_5, undriven_6, undriven_7,
       undriven_8, undriven_9, undriven_10, undriven_11, undriven_12, undriven_13, undriven_14, undriven_15,
       undriven_16, undriven_17, undriven_18, undriven_19, undriven_20, undriven_21, undriven_22,
       undriven_23, undriven_24, undriven_25, undriven_26, undriven_27, undriven_28, undriven_29,
       undriven_30, undriven_31, undriven_32, undriven_33, undriven_34, undriven_35, undriven_36,
       undriven_37, undriven_38, undriven_39, undriven_40, undriven_41, undriven_42, undriven_43,
       undriven_44, undriven_45, undriven_46, undriven_47, undriven_48, undriven_49, undriven_50,
       undriven_51, undriven_52, undriven_53, undriven_54, undriven_55, undriven_56, undriven_57,
       undriven_58, undriven_59, undriven_60, undriven_61, undriven_62, undriven_63, undriven_64,
       undriven_65, undriven_66, undriven_67, undriven_68, undriven_69, undriven_70, undriven_71,
       undriven_72, undriven_73, undriven_74, undriven_75, undriven_76, undriven_77, undriven_78,
       undriven_79, undriven_80, undriven_81, undriven_82, undriven_83, undriven_84, undriven_85,
       undriven_86, undriven_87, undriven_88, undriven_89, undriven_90, undriven_91, undriven_92,
       undriven_93, undriven_94, undriven_95, undriven_96, undriven_97, undriven_98, undriven_99,
       undriven_100, undriven_101, undriven_102, undriven_103, undriven_104, undriven_105, undriven_106,
       undriven_107, undriven_108, undriven_109, undriven_110, undriven_111, undriven_112, undriven_113,
       undriven_114, undriven_115, undriven_116, undriven_117, undriven_118, undriven_119, undriven_120,
       undriven_121, undriven_122, undriven_123, undriven_124, undriven_125, undriven_126, undriven_127,
       undriven_128, undriven_129, undriven_130, undriven_131, undriven_132, undriven_133, undriven_134,
       undriven_135, undriven_136, undriven_137, undriven_138, xor8_1_y0, xor8_1_y1, xor8_1_y2, xor8_1_y3,
       xor8_1_y4, xor8_1_y5, xor8_1_y6, xor8_1_y7, xor_1_y, xor_2_y, xor_3_y, xor_4_y, xor_5_y, xor_6_y,
       xor_7_y, xor_8_y;

  XOR xor_1 (.A(B0), .B(selSUB), .Y(xor_1_y));
  XOR xor_2 (.A(B1), .B(undriven), .Y(xor_2_y));
  XOR xor_3 (.A(B2), .B(undriven_2), .Y(xor_3_y));
  XOR xor_4 (.A(B3), .B(undriven_3), .Y(xor_4_y));
  XOR xor_5 (.A(B4), .B(undriven_4), .Y(xor_5_y));
  XOR xor_6 (.A(B5), .B(undriven_5), .Y(xor_6_y));
  XOR xor_7 (.A(B6), .B(undriven_6), .Y(xor_7_y));
  XOR xor_8 (.A(B7), .B(undriven_7), .Y(xor_8_y));
  ADD8 add8_1 (
    .A0(A0), .A1(A1), .A2(A2), .A3(A3), .A4(A4), .A5(A5), .A6(A6), .A7(A7), .B0(xor_1_y), .B1(xor_2_y),
    .B2(xor_3_y), .B3(xor_4_y), .B4(xor_5_y), .B5(xor_6_y), .B6(xor_7_y), .B7(xor_8_y), .Cin(undriven_8),
    .S0(add8_1_s0), .S1(add8_1_s1), .S2(add8_1_s2), .S3(add8_1_s3), .S4(add8_1_s4), .S5(add8_1_s5),
    .S6(add8_1_s6), .S7(add8_1_s7), .Cout(Cout));
  AND8 and8_1 (
    .A0(undriven_9), .A1(undriven_10), .A2(undriven_11), .A3(undriven_12), .A4(undriven_13),
    .A5(undriven_14), .A6(undriven_15), .A7(undriven_16), .B0(undriven_17), .B1(undriven_18),
    .B2(undriven_19), .B3(undriven_20), .B4(undriven_21), .B5(undriven_22), .B6(undriven_23),
    .B7(undriven_24), .Y0(and8_1_y0), .Y1(and8_1_y1), .Y2(and8_1_y2), .Y3(and8_1_y3), .Y4(and8_1_y4),
    .Y5(and8_1_y5), .Y6(and8_1_y6), .Y7(and8_1_y7));
  XOR8 xor8_1 (
    .A0(undriven_25), .A1(undriven_26), .A2(undriven_27), .A3(undriven_28), .A4(undriven_29),
    .A5(undriven_30), .A6(undriven_31), .A7(undriven_32), .B0(undriven_33), .B1(undriven_34),
    .B2(undriven_35), .B3(undriven_36), .B4(undriven_37), .B5(undriven_38), .B6(undriven_39),
    .B7(undriven_40), .Y0(xor8_1_y0), .Y1(xor8_1_y1), .Y2(xor8_1_y2), .Y3(xor8_1_y3), .Y4(xor8_1_y4),
    .Y5(xor8_1_y5), .Y6(xor8_1_y6), .Y7(xor8_1_y7));
  LSHIFT8 lshift8_1 (
    .A0(undriven_41), .A1(undriven_42), .A2(undriven_43), .A3(undriven_44), .A4(undriven_45),
    .A5(undriven_46), .A6(undriven_47), .A7(undriven_48), .Y0(lshift8_1_y0), .Y1(lshift8_1_y1),
    .Y2(lshift8_1_y2), .Y3(lshift8_1_y3), .Y4(lshift8_1_y4), .Y5(lshift8_1_y5), .Y6(lshift8_1_y6),
    .Y7(lshift8_1_y7));
  RSHIFT8 rshift8_1 (
    .A0(undriven_49), .A1(undriven_50), .A2(undriven_51), .A3(undriven_52), .A4(undriven_53),
    .A5(undriven_54), .A6(undriven_55), .A7(undriven_56), .Y0(rshift8_1_y0), .Y1(rshift8_1_y1),
    .Y2(rshift8_1_y2), .Y3(rshift8_1_y3), .Y4(rshift8_1_y4), .Y5(rshift8_1_y5), .Y6(rshift8_1_y6),
    .Y7(rshift8_1_y7));
  MUX1_8 mux1_8_1 (
    .d0(undriven_57), .d1(add8_1_s0), .d2(and8_1_y0), .d3(xor8_1_y0), .d4(lshift8_1_y0), .d5(rshift8_1_y0),
    .d6(1'b0), .d7(undriven_58), .s0(selADD), .s1(undriven_59), .s2(selAND), .s3(selXOR), .s4(selLSH),
    .s5(selRSH), .s6(undriven_60), .s7(undriven_61), .Y(R0));
  MUX1_8 mux1_8_2 (
    .d0(undriven_62), .d1(add8_1_s1), .d2(and8_1_y1), .d3(xor8_1_y1), .d4(lshift8_1_y1), .d5(rshift8_1_y1),
    .d6(undriven_63), .d7(undriven_64), .s0(undriven_65), .s1(undriven_66), .s2(undriven_67),
    .s3(undriven_68), .s4(undriven_69), .s5(undriven_70), .s6(undriven_71), .s7(undriven_72), .Y(R1));
  MUX1_8 mux1_8_3 (
    .d0(undriven_73), .d1(add8_1_s2), .d2(and8_1_y2), .d3(xor8_1_y2), .d4(lshift8_1_y2), .d5(rshift8_1_y2),
    .d6(undriven_74), .d7(undriven_75), .s0(undriven_76), .s1(undriven_77), .s2(undriven_78),
    .s3(undriven_79), .s4(undriven_80), .s5(undriven_81), .s6(undriven_82), .s7(undriven_83), .Y(R2));
  MUX1_8 mux1_8_4 (
    .d0(undriven_84), .d1(add8_1_s3), .d2(and8_1_y3), .d3(xor8_1_y3), .d4(lshift8_1_y3), .d5(rshift8_1_y3),
    .d6(undriven_85), .d7(undriven_86), .s0(undriven_87), .s1(undriven_88), .s2(undriven_89),
    .s3(undriven_90), .s4(undriven_91), .s5(undriven_92), .s6(undriven_93), .s7(undriven_94), .Y(R3));
  MUX1_8 mux1_8_5 (
    .d0(undriven_95), .d1(add8_1_s4), .d2(and8_1_y4), .d3(xor8_1_y4), .d4(lshift8_1_y4), .d5(rshift8_1_y4),
    .d6(undriven_96), .d7(undriven_97), .s0(undriven_98), .s1(undriven_99), .s2(undriven_100),
    .s3(undriven_101), .s4(undriven_102), .s5(undriven_103), .s6(undriven_104), .s7(undriven_105), .Y(R4));
  MUX1_8 mux1_8_6 (
    .d0(undriven_106), .d1(add8_1_s5), .d2(and8_1_y5), .d3(xor8_1_y5), .d4(lshift8_1_y5), .d5(rshift8_1_y5),
    .d6(undriven_107), .d7(undriven_108), .s0(undriven_109), .s1(undriven_110), .s2(undriven_111),
    .s3(undriven_112), .s4(undriven_113), .s5(undriven_114), .s6(undriven_115), .s7(undriven_116), .Y(R5));
  MUX1_8 mux1_8_7 (
    .d0(undriven_117), .d1(add8_1_s6), .d2(and8_1_y6), .d3(xor8_1_y6), .d4(lshift8_1_y6), .d5(rshift8_1_y6),
    .d6(undriven_118), .d7(undriven_119), .s0(undriven_120), .s1(undriven_121), .s2(undriven_122),
    .s3(undriven_123), .s4(undriven_124), .s5(undriven_125), .s6(undriven_126), .s7(undriven_127), .Y(R6));
  MUX1_8 mux1_8_8 (
    .d0(undriven_128), .d1(add8_1_s7), .d2(and8_1_y7), .d3(xor8_1_y7), .d4(lshift8_1_y7), .d5(rshift8_1_y7),
    .d6(undriven_129), .d7(undriven_130), .s0(undriven_131), .s1(undriven_132), .s2(undriven_133),
    .s3(undriven_134), .s4(undriven_135), .s5(undriven_136), .s6(undriven_137), .s7(undriven_138), .Y(R7));

  // Notes on the sheet:
  //   8-BIT ALU  -  every gate built from transistors (NOT/NAND/NOR), composed hierarchically
  //   Direct one-hot select lines (assert exactly ONE):
  //   selADD  selSUB  selAND  selXOR  selLSH  selRSH   ->  one-hot mux relays the chosen result
  //   A0..A7 / B0..B7 = operand bits (A0=LSB);  R0..R7 = result;  Cout = adder carry (ADD/SUB)
endmodule
